// Logisim project ComputerTest.circ as structural Verilog: 3 circuits, main circuit main
module main (
  input  [25:0] Address,
  input  [31:0] in_2,
  input  [2:0] in_3
);

  wire clock_1_out, dipswitch_1_sw1, dipswitch_1_sw2, not_1_out;
  wire [31:0] ram_1_dout, ram_setter_1_byteout, transistor_1_out;

  DipSwitch #(.number(2)) dipswitch_1 (.sw1(dipswitch_1_sw1), .sw2(dipswitch_1_sw2));
  Clock clock_1 (.out(clock_1_out));
  not not_1 (not_1_out, dipswitch_1_sw2);
  RAM #(.addrWidth(24), .dataWidth(32), .trigger("falling")) ram_1 (
    .addr(Address[25:2]), .we(dipswitch_1_sw1), .oe(dipswitch_1_sw2), .clk(clock_1_out),
    .din(ram_setter_1_byteout), .dout(ram_1_dout));
  Transistor #(.width(32)) transistor_1 (.in(in_2), .out(transistor_1_out), .gate(not_1_out));
  ALU alu_1 ();  // open: func7, rs1, rs2, func3, immediate, rd
  RAM_SETTER ram_setter_1 (
    .DATA(transistor_1_out), .MEMORY(ram_1_dout), .FUNC3(in_3), .BYTELOCATION(Address[1:0]),
    .ByteOut(ram_setter_1_byteout));
endmodule

module ALU (
  input  [6:0] func7,
  input  [31:0] rs1,
  input  [31:0] rs2,
  input  [2:0] func3,
  input  immediate,
  output [31:0] rd
);

  wire and_2_out, comparator_1_gt, comparator_2_gt, not_1_out;
  wire [31:0] adder_1_out, and_1_out, bit_extender_1_out, bit_extender_2_out, multiplexer_1_out,
       multiplexer_2_out, or_1_out, shifter_1_out, shifter_2_out, shifter_3_out, subtractor_1_out, xor_1_out;

  not not_1 (not_1_out, immediate);
  Adder #(.width(32)) adder_1 (.a(rs1), .b(rs2), .out(adder_1_out));  // open: cin, cout
  Subtractor #(.width(32)) subtractor_1 (.a(rs1), .b(rs2), .out(subtractor_1_out));  // open: bin, bout
  Shifter #(.width(32)) shifter_1 (.in(rs2), .\dist (rs2[4:0]), .out(shifter_1_out));
  Comparator #(.width(32)) comparator_1 (.a(rs1), .b(rs2), .gt(comparator_1_gt));  // open: eq, lt
  Comparator #(.mode("unsigned"), .width(32)) comparator_2 (.a(rs2), .b(rs2), .gt(comparator_2_gt));  // open: eq, lt
  assign xor_1_out = rs1 ^ rs2;  // XOR_Gate xor_1, 32 bits wide
  Shifter #(.shift("lr"), .width(32)) shifter_2 (.in(rs1), .\dist (rs2[4:0]), .out(shifter_2_out));
  Shifter #(.shift("ar"), .width(32)) shifter_3 (.in(rs1), .\dist (rs2[4:0]), .out(shifter_3_out));
  assign bit_extender_1_out = {{31{comparator_1_gt}}, comparator_1_gt};  // Bit_Extender bit_extender_1
  assign bit_extender_2_out = {{31{comparator_2_gt}}, comparator_2_gt};  // Bit_Extender bit_extender_2
  assign or_1_out = rs1 | rs2;  // OR_Gate or_1, 32 bits wide
  assign and_1_out = rs1 & rs2;  // AND_Gate and_1, 32 bits wide
  Multiplexer #(.width(32)) multiplexer_1 (
    .in0(adder_1_out), .in1(subtractor_1_out), .out(multiplexer_1_out), .sel(and_2_out));
  Multiplexer #(.width(32)) multiplexer_2 (
    .in0(shifter_2_out), .in1(shifter_3_out), .out(multiplexer_2_out), .sel(and_2_out));
  and and_2 (and_2_out, func7[5], not_1_out);
  Multiplexer #(.select(3), .width(32)) multiplexer_3 (
    .in0(multiplexer_1_out), .in1(shifter_1_out), .in2(bit_extender_1_out), .in3(bit_extender_2_out),
    .in4(xor_1_out), .in5(multiplexer_2_out), .in6(or_1_out), .in7(and_1_out), .out(rd), .sel(func3));
endmodule

module RAM_SETTER (
  input  [31:0] DATA,
  input  [31:0] MEMORY,
  input  [2:0] FUNC3,
  input  [1:0] BYTELOCATION,
  output [31:0] ByteOut
);

  wire [31:0] multiplexer_1_out, multiplexer_2_out, multiplexer_3_out;

  Multiplexer #(.width(32)) multiplexer_1 (
    .in0({MEMORY[31:16], DATA[15:0]}), .in1({DATA[15:0], MEMORY[15:0]}), .out(multiplexer_1_out),
    .sel(BYTELOCATION[1]));
  Multiplexer #(.select(2), .width(32)) multiplexer_2 (
    .in0({MEMORY[31:8], DATA[7:0]}), .in1({MEMORY[31:16], DATA[7:0], MEMORY[7:0]}),
    .in2({MEMORY[31:24], DATA[7:0], MEMORY[15:0]}), .in3({DATA[7:0], MEMORY[23:0]}), .out(multiplexer_2_out),
    .sel(BYTELOCATION));
  Multiplexer #(.select(3), .width(32)) multiplexer_3 (
    .in0(multiplexer_2_out), .in1(multiplexer_1_out), .in2(DATA), .out(multiplexer_3_out), .sel(FUNC3));  // open: in3, in4, in5, in6, in7
  assign ByteOut = {32{1'b0}} | multiplexer_3_out;  // OR_Gate or_1, 32 bits wide
endmodule
